# Fritzing sketch Leak Detector (saved by Fritzing 1.0.2b)
breadboards: 1

parts:
  M3 = Arduino Nano 33 IOT-smd
  LED1 = smd LED [color="Green (555nm)" package="0805 [SMD]"]
  LED2 = smd LED [color="Red (633nm)" package="0805 [SMD]"]
  R1 = Resistor [tolerance=±5% power=0.25W resistance=220 package=THT]
  R2 = Resistor [tolerance=±5% power=0.25W resistance=220 package=THT]
  Water_Level_Sensor1 = Water Level Sensor [package=board]
  Q1 = PNP-Transistor [package="TO92 [THT]"]
  R3 = Resistor [tolerance=±5% power=0.25W resistance=220 package=THT]
  J1 = Piezo Speaker

nets:
  N1: M3.pin_1, J1.pin2
  N2: M3.pin_3, Water_Level_Sensor1.SIG
  N3: M3.pin_13, M3.pin_18
  N4: M3.pin_14, M3.pin_19
  N5: M3.pin_20, R1.Pin_0, R2.Pin_0, Water_Level_Sensor1.GND, Q1.B
  N6: M3.pin_21, Water_Level_Sensor1.VCC
  N7: M3.pin_22, LED2.cathode
  N8: M3.pin_23, LED1.cathode
  N9: M3.pin_24, R3.Pin_1
  N10: LED1.anode, R2.Pin_1
  N11: LED2.anode, R1.Pin_1
  N12: Q1.E, J1.pin1
  N13: Q1.C, R3.Pin_0

custom parts:
  Arduino Nano 33 IOT-smd: The Arduino Nano 33 IoT is the easiest and cheapest point of entry to enhance existing devices (and creating new ones) to be part of the IoT and designing pico-network applications. Whether you are looking at building a sensor network connected to your office or home router, or if you want to create a BLE device sending data to a cellphone, the Nano 33 IoT is your one-stop-solution for many of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
  Water Level Sensor: A water level sensor. This sensor operates at 3V to 5V. The Sig (signal) pin outputs an analogue signal that is in proportion to the amount of water in contact with the sensor.
